# Fritzing sketch Parking_sensors (saved by Fritzing 0.9.3b)
breadboards: 1

parts:
  Part1 = Arduino Uno (Rev3)
  Part2 = KY-012 Active Buzzer Module [package="Breakout board"]
  hc-sr1 = hc-sr04
  hc-sr2 = hc-sr04
  hc-sr3 = hc-sr04
  hc-sr4 = hc-sr04
  LCM1602_IIC2 = LCM1602 IIC [part_number="LCM1602 IIC" chip_label="LCM1602 IIC" package="DIP (Dual Inline) [THT]"]
  LCD1 = LCD screen

nets:
  N1: Part1.A4/SDA, LCM1602_IIC2.SDA
  N2: Part1.A5/SCL, LCM1602_IIC2.SCL
  N3: Part1.D8, hc-sr2.Echo
  N4: Part1.D9_PWM, hc-sr2.Trig
  N5: Part1.D10_PWM/SS, hc-sr1.Echo
  N6: Part1.D11_PWM/MOSI, hc-sr1.Trig
  N7: Part1.D4, hc-sr4.Echo
  N8: Part1.D5_PWM, hc-sr4.Trig
  N9: Part1.D6_PWM, hc-sr3.Echo
  N10: Part1.D7, hc-sr3.Trig
  VCC: Part1.5V, Part2.S, hc-sr2.VCC, hc-sr3.VCC, hc-sr4.VCC, LCM1602_IIC2.VCC
  GND: Part1.GND, Part2.-, hc-sr1.GND, hc-sr2.GND, hc-sr3.GND, hc-sr4.GND, LCM1602_IIC2.GND
  VSS: LCM1602_IIC2.VSS, LCD1.VSS
  VDD: LCM1602_IIC2.VDD, LCD1.VDD
  N11: LCM1602_IIC2.V0, LCD1.V0
  N12: LCM1602_IIC2.RS, LCD1.RS
  N13: LCM1602_IIC2.RW, LCD1.R/W
  N14: LCM1602_IIC2.E, LCD1.E
  N15: LCM1602_IIC2.D0, LCD1.DB0
  N16: LCM1602_IIC2.D1, LCD1.DB1
  N17: LCM1602_IIC2.D2, LCD1.DB2
  N18: LCM1602_IIC2.D3, LCD1.DB3
  N19: LCM1602_IIC2.D4, LCD1.DB4
  N20: LCM1602_IIC2.D5, LCD1.DB5
  N21: LCM1602_IIC2.D6, LCD1.DB6
  N22: LCM1602_IIC2.D7, LCD1.DB7
  N23: LCM1602_IIC2.A, LCD1.LED+
  N24: LCM1602_IIC2.K, LCD1.LED-

custom parts:
  KY-012 Active Buzzer Module: Active Piezoelectric Buzzer Module Keyes KY-012, it produces single-tone sound when signal is high.
  LCM1602 IIC: I2C-Module to use a 1602 or 2004 LCD on with the wire.h libory Serial LCD Modul
